# Fritzing sketch Nano lysimiter v1 (saved by Fritzing 0.9.2b)

parts:
  A = Arduino Nano (Rev3.0)
  MAX232_TTL_3_3v = RS232 Transceiver [package=so016]
  Relay = Jtron 1 Channel Optoisolated Relay Module [package=relay]
  Solenoid_valve_-_12v = Solenoid
  Power_plug_-_DC_5_v = Power plug
  Power_plug_-_DC_12_v = Power plug
  S1 = SWITCH-MOMENTARY-2 [package=tactile_switch_smd-2]
  S2 = SWITCH-MOMENTARY-2 [package=tactile_switch_smd-2]
  R1 = Resistor [tolerance=±5% resistance=10k package="2512 [SMD]"]

nets (from the schematic view):
  N1: A.D0/RX, MAX232_TTL_3_3v.T1OUT
  GND: A.GND, MAX232_TTL_3_3v.C1+, Relay.IN1, Power_plug_-_DC_5_v.GND
  N2: A.D2, S2.1
  N3: A.D3, S1.1
  VIN: A.VIN, Power_plug_-_DC_5_v.VCC
  5V: A.5V, Relay.VCC, R1.Pin_1
  3V3: A.3V3, MAX232_TTL_3_3v.VCC
  N4: Relay.NC, Solenoid_valve_-_12v.pin1, Power_plug_-_DC_12_v.GND
  N5: Relay.NO, Solenoid_valve_-_12v.pin2, Power_plug_-_DC_12_v.VCC
  N6: S1.2, S2.2, R1.Pin_0

notes:
  A
